# Fritzing sketch esp8266_board (saved by Fritzing 0.9.2b)
circuit board: 8.33489cm x 4.21259cm
breadboards: 1

parts:
  Reset = Momentary Switch [package=ksa_sealed_tac_switch]
  R1 = Resistor [tolerance=±5% resistance=10k package=THT]
  R2 = Resistor [tolerance=±5% resistance=10k package=THT]
  R3 = Resistor [tolerance=±5% resistance=10k package=THT]
  C1 = Ceramic Capacitor [capacitance=100nF package="100 mil [THT, multilayer]"]
  C3 = Ceramic Capacitor [capacitance=100nF package="100 mil [THT, multilayer]"]
  Q1 = NPN-Transistor [package="TO92 [THT]"]
  Q2 = NPN-Transistor [package="TO92 [THT]"]
  R4 = Resistor [tolerance=±5% resistance=10k package=THT]
  R5 = Resistor [tolerance=±5% resistance=10k package=THT]
  R6 = Resistor [tolerance=±5% resistance=470 package=THT]
  R7 = Resistor [tolerance=±5% resistance=470 package=THT]
  LED1 = LEDs [package=led10mm]
  R9 = Resistor [tolerance=±5% resistance=470 package=THT]
  I/O = female pin header, 4 pins [form="♀ (female)"]
  POWER = female pin header, 2 pins [form="♀ (female)"]
  UART = male pin header, 6 pins [form="♂ (male)"]
  C2 = Electrolytic Capacitor [capacitance=0.1mF package="100 mil [THT, electrolytic]"]
  U1 = ESP8266 WiFi Module [part_number=ESP8266]
  R8 = Resistor [tolerance=±5% resistance=0 package=THT]
  Firmware_Update = Momentary Switch [package=ksa_sealed_tac_switch]

nets:
  N1: Reset.1, Reset.2, R7.Pin_1, R8.Pin_1
  GND: Reset.3, Reset.4, C1.0, C3.0, I/O.pin2, POWER.pin2, UART.pin5, C2.-, U1.GND, Firmware_Update.3, Firmware_Update.4
  3.3V/CH_PD: R1.Pin_0, R2.Pin_0, R3.Pin_0, C3.1, R9.Pin_0, I/O.pin1, POWER.pin1, UART.pin1, C2.+, U1.VCC, U1.CH_PD
  GPIO0: R1.Pin_1, Q2.C, R6.Pin_0, I/O.pin4, U1.GPIO_0
  GPIO2: R2.Pin_1, I/O.pin3, U1.GPIO_2
  nRST: R3.Pin_1, C1.1
  RTS: Q1.E, R5.Pin_1, UART.pin4
  N2: Q1.B, R4.Pin_0
  nRTS: Q1.C, R7.Pin_0
  DTR: Q2.E, R4.Pin_1, UART.pin3
  N3: Q2.B, R5.Pin_0
  N4: R6.Pin_1, Firmware_Update.1, Firmware_Update.2
  N5: LED1.A, R9.Pin_1
  RESET: LED1.C, U1.GPIO_16, R8.Pin_0
  RXD: UART.pin2, U1.RXD
  TXD: UART.pin6, U1.TXD

notes:
  ESP8266 I/O BOARD, The In/Out board extension to ESP-01 ESP8266 module, 1.0
  IN
  OUT

custom parts:
  ESP8266 WiFi Module: Generic WiFi Module based on the ESP8266 with onboard PCB antenna and UART communications
